// Digital circuit frontpanel.dig as structural Verilog
module frontpanel (
  input  [7:0] value,
  input  [1:0] dest,
  input  [1:0] src,
  input  tworeg,
  output [31:0] R0,
  output [31:0] R1,
  output [31:0] R2,
  output [31:0] R3,
  output [3:0] PC
);

  wire add, add_out, advance_out, assembler_1_p10, hex, hexdisplay_1_p1, hexdisplay_1_p2, hexdisplay_1_p3,
       hexdisplay_1_p4, hexdisplay_1_p5, hexdisplay_1_p6, hexdisplay_1_p7, hexdisplay_1_p8, hexdisplay_1_p9,
       hexdisplay_1_p10, hexdisplay_2_p1, hexdisplay_2_p2, hexdisplay_2_p3, hexdisplay_2_p4, hexdisplay_2_p5,
       hexdisplay_2_p6, hexdisplay_2_p7, hexdisplay_2_p8, hexdisplay_2_p9, hexdisplay_2_p10,
       instrdisplay_1_p1, instrdisplay_1_p2, instrdisplay_1_p3, instrdisplay_1_p4, instrdisplay_1_p5,
       instrdisplay_1_p6, jump, jump_out, mode_out, move, move_out, not_1_out, pmshim_1_p6, pmshim_1_p7,
       pmshim_1_p8, regdisplay_1_p1, regdisplay_1_p2, regdisplay_2_p1, regdisplay_2_p2, tworeg_t;
  wire [1:0] decoder_1_result_mux, rd, rs;
  wire [2:0] op;
  wire [3:0] hexdisplay_1_d1, hexdisplay_1_d2, hexdisplay_1_d3, hexdisplay_1_d4, hexdisplay_1_d5,
       hexdisplay_1_d6, hexdisplay_1_d7, hexdisplay_1_d8, hexdisplay_1_d9, hexdisplay_1_d10, hexdisplay_2_d1,
       hexdisplay_2_d2, hexdisplay_2_d3, hexdisplay_2_d4, hexdisplay_2_d5, hexdisplay_2_d6, hexdisplay_2_d7,
       hexdisplay_2_d8, hexdisplay_2_d9, hexdisplay_2_d10, pmshim_1_p4;
  wire [15:0] assembler_1_p9, fetch_1_instr_o, instrdisplay_1_d1, instrdisplay_1_d2, instrdisplay_1_d3,
       instrdisplay_1_d4, instrdisplay_1_d5, instrdisplay_1_d6, pmshim_1_p5, Program_d, regdisplay_1_d1,
       regdisplay_1_d2, regdisplay_2_d1, regdisplay_2_d2;
  wire [31:0] execute_1_result, L, R, regfile_1_rdval, regfile_1_rsval;

  Button u_add (.out(add_out));
  Button u_move (.out(move_out));
  Button u_jump (.out(jump_out));
  LED programming (.in(mode_out));
  DipSwitch mode (.out(mode_out));
  // assembler assembler_1: pin names not known; wires that end beside it: mode_out, value, dest, src, tworeg, add_out, move_out, jump_out, assembler_1_p9, assembler_1_p10
  SixteenSeg sixteenseg_1 (.led(regdisplay_1_d1), .dp(regdisplay_1_p1));
  SixteenSeg sixteenseg_2 (.led(regdisplay_1_d2), .dp(regdisplay_1_p2));
  regdisplay regdisplay_1 (
    .D1(regdisplay_1_d1), .P1(regdisplay_1_p1), .D2(regdisplay_1_d2), .P2(regdisplay_1_p2), .E(1'b1),
    .J(jump), .R(rd));
  Seven_Seg_Hex seven_seg_hex_1 (.d(hexdisplay_1_d1), .dp(hexdisplay_1_p1));
  DipSwitch u_hex (.out(hex));
  // pmshim pmshim_1: pin names not known; wires that end beside it: PC, assembler_1_p9, assembler_1_p10, pmshim_1_p4, pmshim_1_p5, pmshim_1_p6, pmshim_1_p7, pmshim_1_p8
  Seven_Seg_Hex seven_seg_hex_2 (.d(hexdisplay_1_d2), .dp(hexdisplay_1_p2));
  Seven_Seg_Hex seven_seg_hex_3 (.d(hexdisplay_1_d3), .dp(hexdisplay_1_p3));
  hexdisplay hexdisplay_1 (
    .D1(hexdisplay_1_d1), .P1(hexdisplay_1_p1), .D2(hexdisplay_1_d2), .P2(hexdisplay_1_p2),
    .D3(hexdisplay_1_d3), .P3(hexdisplay_1_p3), .D4(hexdisplay_1_d4), .P4(hexdisplay_1_p4),
    .D5(hexdisplay_1_d5), .P5(hexdisplay_1_p5), .D6(hexdisplay_1_d6), .P6(hexdisplay_1_p6),
    .D7(hexdisplay_1_d7), .P7(hexdisplay_1_p7), .D8(hexdisplay_1_d8), .P8(hexdisplay_1_p8),
    .D9(hexdisplay_1_d9), .P9(hexdisplay_1_p9), .D10(hexdisplay_1_d10), .P10(hexdisplay_1_p10),
    .E(not_1_out), .V(L), .H(hex));
  not not_1 (not_1_out, jump);
  EEPROMDualPort #(.AddrBits(4), .Bits(16)) Program (
    .A(pmshim_1_p4), .Din(pmshim_1_p5), .str(pmshim_1_p6), .C(pmshim_1_p7), .ld(pmshim_1_p8), .D(Program_d));
  Button advance (.out(advance_out));
  Seven_Seg_Hex seven_seg_hex_4 (.d(hexdisplay_1_d4), .dp(hexdisplay_1_p4));
  Seven_Seg_Hex seven_seg_hex_5 (.d(hexdisplay_1_d5), .dp(hexdisplay_1_p5));
  Seven_Seg_Hex seven_seg_hex_6 (.d(hexdisplay_1_d6), .dp(hexdisplay_1_p6));
  Seven_Seg_Hex seven_seg_hex_7 (.d(hexdisplay_1_d7), .dp(hexdisplay_1_p7));
  fetch fetch_1 (
    .prog(mode_out), .bypass(assembler_1_p9), .Instr_i(Program_d), .clock(advance_out), .value(R),
    .jump(jump), .pc(PC), .instr_o(fetch_1_instr_o));
  Seven_Seg_Hex seven_seg_hex_8 (.d(hexdisplay_1_d8), .dp(hexdisplay_1_p8));
  Seven_Seg_Hex seven_seg_hex_9 (.d(hexdisplay_1_d9), .dp(hexdisplay_1_p9));
  Seven_Seg_Hex seven_seg_hex_10 (.d(hexdisplay_1_d10), .dp(hexdisplay_1_p10));
  decoder decoder_1 (
    .rdval(regfile_1_rdval), .rsval(regfile_1_rsval), .Instr(fetch_1_instr_o), .rs(rs), .rd(rd),
    .result_mux(decoder_1_result_mux), .L(L), .R(R), .tworeg(tworeg_t), .move(move), .add(add), .op(op),
    .jump(jump));
  SixteenSeg sixteenseg_3 (.led(instrdisplay_1_d1), .dp(instrdisplay_1_p1));
  SixteenSeg sixteenseg_4 (.led(instrdisplay_1_d2), .dp(instrdisplay_1_p2));
  instrdisplay instrdisplay_1 (
    .D1(instrdisplay_1_d1), .P1(instrdisplay_1_p1), .D2(instrdisplay_1_d2), .P2(instrdisplay_1_p2),
    .D3(instrdisplay_1_d3), .P3(instrdisplay_1_p3), .D4(instrdisplay_1_d4), .P4(instrdisplay_1_p4),
    .D5(instrdisplay_1_d5), .P5(instrdisplay_1_p5), .D6(instrdisplay_1_d6), .P6(instrdisplay_1_p6), .I(op));
  SixteenSeg sixteenseg_5 (.led(instrdisplay_1_d3), .dp(instrdisplay_1_p3));
  SixteenSeg sixteenseg_6 (.led(instrdisplay_1_d4), .dp(instrdisplay_1_p4));
  SixteenSeg sixteenseg_7 (.led(instrdisplay_1_d5), .dp(instrdisplay_1_p5));
  SixteenSeg sixteenseg_8 (.led(instrdisplay_1_d6), .dp(instrdisplay_1_p6));
  Seven_Seg_Hex seven_seg_hex_11 (.d(hexdisplay_2_d1), .dp(hexdisplay_2_p1));
  execute execute_1 (.result_mux(decoder_1_result_mux), .L(L), .R(R), .result(execute_1_result));
  Seven_Seg_Hex seven_seg_hex_12 (.d(hexdisplay_2_d2), .dp(hexdisplay_2_p2));
  Seven_Seg_Hex seven_seg_hex_13 (.d(hexdisplay_2_d3), .dp(hexdisplay_2_p3));
  hexdisplay hexdisplay_2 (
    .D1(hexdisplay_2_d1), .P1(hexdisplay_2_p1), .D2(hexdisplay_2_d2), .P2(hexdisplay_2_p2),
    .D3(hexdisplay_2_d3), .P3(hexdisplay_2_p3), .D4(hexdisplay_2_d4), .P4(hexdisplay_2_p4),
    .D5(hexdisplay_2_d5), .P5(hexdisplay_2_p5), .D6(hexdisplay_2_d6), .P6(hexdisplay_2_p6),
    .D7(hexdisplay_2_d7), .P7(hexdisplay_2_p7), .D8(hexdisplay_2_d8), .P8(hexdisplay_2_p8),
    .D9(hexdisplay_2_d9), .P9(hexdisplay_2_p9), .D10(hexdisplay_2_d10), .P10(hexdisplay_2_p10), .E(1'b1),
    .V(R), .H(hex));
  Seven_Seg_Hex seven_seg_hex_14 (.d(hexdisplay_2_d4), .dp(hexdisplay_2_p4));
  Seven_Seg_Hex seven_seg_hex_15 (.d(hexdisplay_2_d5), .dp(hexdisplay_2_p5));
  regfile regfile_1 (
    .rs(rs), .rd(rd), .result(execute_1_result), .clock(advance_out), .rdval(regfile_1_rdval),
    .rsval(regfile_1_rsval), .R0(R0), .R1(R1), .R2(R2), .R3(R3));
  Seven_Seg_Hex seven_seg_hex_16 (.d(hexdisplay_2_d6), .dp(hexdisplay_2_p6));
  Seven_Seg_Hex seven_seg_hex_17 (.d(hexdisplay_2_d7), .dp(hexdisplay_2_p7));
  Seven_Seg_Hex seven_seg_hex_18 (.d(hexdisplay_2_d8), .dp(hexdisplay_2_p8));
  Seven_Seg_Hex seven_seg_hex_19 (.d(hexdisplay_2_d9), .dp(hexdisplay_2_p9));
  Seven_Seg_Hex seven_seg_hex_20 (.d(hexdisplay_2_d10), .dp(hexdisplay_2_p10));
  SixteenSeg sixteenseg_9 (.led(regdisplay_2_d1), .dp(regdisplay_2_p1));
  SixteenSeg sixteenseg_10 (.led(regdisplay_2_d2), .dp(regdisplay_2_p2));
  regdisplay regdisplay_2 (
    .D1(regdisplay_2_d1), .P1(regdisplay_2_p1), .D2(regdisplay_2_d2), .P2(regdisplay_2_p2), .E(tworeg_t),
    .J(1'b0), .R(rs));

  // Notes on the sheet:
  //   contents of Program (hex, n*v repeats v):
  //   120,161,1bd,191,17d,10e
endmodule
