// Digital circuit hexdisplay.dig as structural Verilog
module hexdisplay (
  input  E,
  input  [31:0] V,
  input  H,
  output [3:0] D1,
  output P1,
  output [3:0] D2,
  output P2,
  output [3:0] D3,
  output P3,
  output [3:0] D4,
  output P4,
  output [3:0] D5,
  output P5,
  output [3:0] D6,
  output P6,
  output [3:0] D7,
  output P7,
  output [3:0] D8,
  output P8,
  output [3:0] D9,
  output P9,
  output [3:0] D10,
  output P10
);

  wire and_1_out, and_2_out, and_3_out, and_4_out, and_5_out, and_6_out, and_7_out, and_8_out, and_9_out,
       comparator_1_gt, comparator_2_gt, comparator_3_gt, comparator_4_gt, comparator_5_gt, comparator_6_gt,
       comparator_7_gt, comparator_8_gt, comparator_9_gt, or_1_out, or_2_out, or_3_out, or_4_out, or_5_out,
       or_6_out, or_7_out, or_8_out, or_9_out;
  wire [3:0] multiplexer_1_out, multiplexer_1_out_2, multiplexer_1_out_3, multiplexer_1_out_4,
       multiplexer_1_out_5, multiplexer_1_out_6, priorityencoder_1_num;
  wire [39:0] bin2bcd_1_o;
  wire [39:24] multiplexer_1_out_7;

  Comparator #(.Bits(4)) comparator_1 (.a(priorityencoder_1_num), .b(4'b1000), .gt(comparator_1_gt));  // open: eq, lt
  and and_1 (and_1_out, comparator_1_gt, E);
  assign D1 = and_1_out ? multiplexer_1_out_7[39:36] : 4'bz;  // Driver driver_1
  or or_1 (or_1_out, multiplexer_1_out_7[36], multiplexer_1_out_7[37], multiplexer_1_out_7[38], multiplexer_1_out_7[39]);
  Comparator #(.Bits(4)) comparator_2 (.a(priorityencoder_1_num), .b(4'b0111), .gt(comparator_2_gt));  // open: eq, lt
  and and_2 (and_2_out, comparator_2_gt, E);
  Comparator #(.Bits(4)) comparator_3 (.a(priorityencoder_1_num), .b(4'b0110), .gt(comparator_3_gt));  // open: eq, lt
  assign D2 = and_2_out ? multiplexer_1_out_7[35:32] : 4'bz;  // Driver driver_2
  and and_3 (and_3_out, comparator_3_gt, E);
  or or_2 (or_2_out, multiplexer_1_out_7[32], multiplexer_1_out_7[33], multiplexer_1_out_7[34], multiplexer_1_out_7[35]);
  assign D3 = and_3_out ? multiplexer_1_out_7[31:28] : 4'bz;  // Driver driver_3
  or or_3 (or_3_out, multiplexer_1_out_7[28], multiplexer_1_out_7[29], multiplexer_1_out_7[30], multiplexer_1_out_7[31]);
  Comparator #(.Bits(4)) comparator_4 (.a(priorityencoder_1_num), .b(4'b0101), .gt(comparator_4_gt));  // open: eq, lt
  and and_4 (and_4_out, comparator_4_gt, E);
  Comparator #(.Bits(4)) comparator_5 (.a(priorityencoder_1_num), .b(4'b0100), .gt(comparator_5_gt));  // open: eq, lt
  assign D4 = and_4_out ? multiplexer_1_out_7[27:24] : 4'bz;  // Driver driver_4
  and and_5 (and_5_out, comparator_5_gt, E);
  or or_4 (or_4_out, multiplexer_1_out_7[24], multiplexer_1_out_7[25], multiplexer_1_out_7[26], multiplexer_1_out_7[27]);
  assign D5 = and_5_out ? multiplexer_1_out_6 : 4'bz;  // Driver driver_5
  or or_5 (or_5_out, multiplexer_1_out_6[0], multiplexer_1_out_6[1], multiplexer_1_out_6[2], multiplexer_1_out_6[3]);
  Comparator #(.Bits(4)) comparator_6 (.a(priorityencoder_1_num), .b(4'b0011), .gt(comparator_6_gt));  // open: eq, lt
  and and_6 (and_6_out, comparator_6_gt, E);
  Comparator #(.Bits(4)) comparator_7 (.a(priorityencoder_1_num), .b(4'b0010), .gt(comparator_7_gt));  // open: eq, lt
  assign D6 = and_6_out ? multiplexer_1_out_5 : 4'bz;  // Driver driver_6
  and and_7 (and_7_out, comparator_7_gt, E);
  or or_6 (or_6_out, multiplexer_1_out_5[0], multiplexer_1_out_5[1], multiplexer_1_out_5[2], multiplexer_1_out_5[3]);
  assign D7 = and_7_out ? multiplexer_1_out_4 : 4'bz;  // Driver driver_7
  or or_7 (or_7_out, multiplexer_1_out_4[0], multiplexer_1_out_4[1], multiplexer_1_out_4[2], multiplexer_1_out_4[3]);
  Comparator #(.Bits(4)) comparator_8 (.a(priorityencoder_1_num), .b(4'b0001), .gt(comparator_8_gt));  // open: eq, lt
  and and_8 (and_8_out, comparator_8_gt, E);
  Comparator #(.Bits(4)) comparator_9 (.a(priorityencoder_1_num), .b(4'b0000), .gt(comparator_9_gt));  // open: eq, lt
  assign D8 = and_8_out ? multiplexer_1_out_3 : 4'bz;  // Driver driver_8
  and and_9 (and_9_out, comparator_9_gt, E);
  or or_8 (or_8_out, multiplexer_1_out_3[0], multiplexer_1_out_3[1], multiplexer_1_out_3[2], multiplexer_1_out_3[3]);
  assign D9 = and_9_out ? multiplexer_1_out_2 : 4'bz;  // Driver driver_9
  or or_9 (or_9_out, multiplexer_1_out_2[0], multiplexer_1_out_2[1], multiplexer_1_out_2[2], multiplexer_1_out_2[3]);
  assign D10 = E ? multiplexer_1_out : 4'bz;  // Driver driver_10
  bin2bcd bin2bcd_1 (.I(V), .O(bin2bcd_1_o));
  PriorityEncoder #(.Selector_Bits(4)) priorityencoder_1 (
    .in0(1'b0), .in1(or_9_out), .in2(or_8_out), .in3(or_7_out), .in4(or_6_out), .in5(or_5_out),
    .in6(or_4_out), .in7(or_3_out), .in8(or_2_out), .in9(or_1_out), .in10(1'b0), .in11(1'b0), .in12(1'b0),
    .in13(1'b0), .in14(1'b0), .in15(1'b0), .num(priorityencoder_1_num));  // open: any
  Multiplexer #(.Bits(40)) multiplexer_1 (
    .sel(H), .in_0(bin2bcd_1_o), .in_1({{8{1'b0}}, V}),
    .out({multiplexer_1_out_7, multiplexer_1_out_6, multiplexer_1_out_5, multiplexer_1_out_4, multiplexer_1_out_3, multiplexer_1_out_2, multiplexer_1_out}));

  assign P1 = 1'b0;
  assign P2 = 1'b0;
  assign P3 = 1'b0;
  assign P4 = 1'b0;
  assign P5 = 1'b0;
  assign P6 = 1'b0;
  assign P7 = 1'b0;
  assign P8 = 1'b0;
  assign P9 = 1'b0;
  assign P10 = 1'b0;
endmodule
