// Digital circuit instrdisplay.dig as structural Verilog
module instrdisplay (
  input  [2:0] I,
  output [15:0] D1,
  output P1,
  output [15:0] D2,
  output P2,
  output [15:0] D3,
  output P3,
  output [15:0] D4,
  output P4,
  output [15:0] D5,
  output P5,
  output [15:0] D6,
  output P6
);

  wire [6:0] multiplexer_1_out, multiplexer_2_out, multiplexer_3_out, multiplexer_4_out, multiplexer_5_out,
       multiplexer_6_out;

  Multiplexer #(.Selector_Bits(3), .Bits(7)) multiplexer_1 (
    .sel(I), .in_0(7'b0100000), .in_1(7'b0100000), .in_2(7'b0100000), .in_3(7'b0100000), .in_4(7'b0100000),
    .in_5(7'b0100000), .in_6(7'b0100000), .in_7(7'b0100000), .out(multiplexer_1_out));
  ROM #(.bigEndian("true"), .AddrBits(7), .Bits(16)) ASCII (.A(multiplexer_1_out), .sel(1'b1), .D(D1));
  Multiplexer #(.Selector_Bits(3), .Bits(7)) multiplexer_2 (
    .sel(I), .in_0(7'b0100000), .in_1(7'b0100000), .in_2(7'b0100000), .in_3(7'b0100000), .in_4(7'b0100000),
    .in_5(7'b0100000), .in_6(7'b0100000), .in_7(7'b0100000), .out(multiplexer_2_out));
  ROM #(.bigEndian("true"), .AddrBits(7), .Bits(16)) ASCII_2 (.A(multiplexer_2_out), .sel(1'b1), .D(D2));
  Multiplexer #(.Selector_Bits(3), .Bits(7)) multiplexer_3 (
    .sel(I), .in_0(7'b0100000), .in_1(7'b0100000), .in_2(7'b0100000), .in_3(7'b0100000), .in_4(7'b0100000),
    .in_5(7'b0100000), .in_6(7'b1001101), .in_7(7'b1001010), .out(multiplexer_3_out));
  ROM #(.bigEndian("true"), .AddrBits(7), .Bits(16)) ASCII_3 (.A(multiplexer_3_out), .sel(1'b1), .D(D3));
  Multiplexer #(.Selector_Bits(3), .Bits(7)) multiplexer_4 (
    .sel(I), .in_0(7'b1000001), .in_1(7'b0100000), .in_2(7'b0100000), .in_3(7'b0100000), .in_4(7'b0100000),
    .in_5(7'b0100000), .in_6(7'b1001111), .in_7(7'b1010101), .out(multiplexer_4_out));
  ROM #(.bigEndian("true"), .AddrBits(7), .Bits(16)) ASCII_4 (.A(multiplexer_4_out), .sel(1'b1), .D(D4));
  Multiplexer #(.Selector_Bits(3), .Bits(7)) multiplexer_5 (
    .sel(I), .in_0(7'b1000100), .in_1(7'b0100000), .in_2(7'b0100000), .in_3(7'b0100000), .in_4(7'b0100000),
    .in_5(7'b0100000), .in_6(7'b1010110), .in_7(7'b1001101), .out(multiplexer_5_out));
  ROM #(.bigEndian("true"), .AddrBits(7), .Bits(16)) ASCII_5 (.A(multiplexer_5_out), .sel(1'b1), .D(D5));
  Multiplexer #(.Selector_Bits(3), .Bits(7)) multiplexer_6 (
    .sel(I), .in_0(7'b1000100), .in_1(7'b0100000), .in_2(7'b0100000), .in_3(7'b0100000), .in_4(7'b0100000),
    .in_5(7'b0100000), .in_6(7'b1000101), .in_7(7'b1010000), .out(multiplexer_6_out));
  ROM #(.bigEndian("true"), .AddrBits(7), .Bits(16)) ASCII_6 (.A(multiplexer_6_out), .sel(1'b1), .D(D6));

  assign P1 = 1'b0;
  assign P2 = 1'b0;
  assign P3 = 1'b0;
  assign P4 = 1'b0;
  assign P5 = 1'b0;
  assign P6 = 1'b0;

  // Notes on the sheet:
  //   contents of ASCII (hex, n*v repeats v):
  //   90ff,c,377,33f,38c,3bb,3fb,f,3ff,3bf,3cf,4a3f,f3,483f,3f3,1c3
  //   ,17*0,4800,4*0,2d79,4*0,4b00,0,300,0,0,90ff,c,377,33f,38c,3bb
  //   ,3fb,f,3ff,3bf,0,0,3000,0,8400,0,0,3cf,4a3f,f3,483f,3f3,1c3,2fb
  //   ,3cc,4833,7c,31c0,f0,14cc,24cc,ff,3c7,20ff,23c7,3bb,4803,fc,90c0
  //   ,a0cc,b400,5400,9033,0,0,0,a000
  //   contents of ASCII_2 (hex, n*v repeats v):
  //   90ff,c,377,33f,38c,3bb,3fb,f,3ff,3bf,3cf,4a3f,f3,483f,3f3,1c3
  //   ,17*0,4800,4*0,2d79,4*0,4b00,0,300,0,0,90ff,c,377,33f,38c,3bb
  //   ,3fb,f,3ff,3bf,0,0,3000,0,8400,0,0,3cf,4a3f,f3,483f,3f3,1c3,2fb
  //   ,3cc,4833,7c,31c0,f0,14cc,24cc,ff,3c7,20ff,23c7,3bb,4803,fc,90c0
  //   ,a0cc,b400,5400,9033,0,0,0,a000
  //   contents of ASCII_3 (hex, n*v repeats v):
  //   90ff,c,377,33f,38c,3bb,3fb,f,3ff,3bf,3cf,4a3f,f3,483f,3f3,1c3
  //   ,17*0,4800,4*0,2d79,4*0,4b00,0,300,0,0,90ff,c,377,33f,38c,3bb
  //   ,3fb,f,3ff,3bf,0,0,3000,0,8400,0,0,3cf,4a3f,f3,483f,3f3,1c3,2fb
  //   ,3cc,4833,7c,31c0,f0,14cc,24cc,ff,3c7,20ff,23c7,3bb,4803,fc,90c0
  //   ,a0cc,b400,5400,9033,0,0,0,a000
  //   contents of ASCII_4 (hex, n*v repeats v):
  //   90ff,c,377,33f,38c,3bb,3fb,f,3ff,3bf,3cf,4a3f,f3,483f,3f3,1c3
  //   ,17*0,4800,4*0,2d79,4*0,4b00,0,300,0,0,90ff,c,377,33f,38c,3bb
  //   ,3fb,f,3ff,3bf,0,0,3000,0,8400,0,0,3cf,4a3f,f3,483f,3f3,1c3,2fb
  //   ,3cc,4833,7c,31c0,f0,14cc,24cc,ff,3c7,20ff,23c7,3bb,4803,fc,90c0
  //   ,a0cc,b400,5400,9033,0,0,0,a000
  //   contents of ASCII_5 (hex, n*v repeats v):
  //   90ff,c,377,33f,38c,3bb,3fb,f,3ff,3bf,3cf,4a3f,f3,483f,3f3,1c3
  //   ,17*0,4800,4*0,2d79,4*0,4b00,0,300,0,0,90ff,c,377,33f,38c,3bb
  //   ,3fb,f,3ff,3bf,0,0,3000,0,8400,0,0,3cf,4a3f,f3,483f,3f3,1c3,2fb
  //   ,3cc,4833,7c,31c0,f0,14cc,24cc,ff,3c7,20ff,23c7,3bb,4803,fc,90c0
  //   ,a0cc,b400,5400,9033,0,0,0,a000
  //   contents of ASCII_6 (hex, n*v repeats v):
  //   90ff,c,377,33f,38c,3bb,3fb,f,3ff,3bf,3cf,4a3f,f3,483f,3f3,1c3
  //   ,17*0,4800,4*0,2d79,4*0,4b00,0,300,0,0,90ff,c,377,33f,38c,3bb
  //   ,3fb,f,3ff,3bf,0,0,3000,0,8400,0,0,3cf,4a3f,f3,483f,3f3,1c3,2fb
  //   ,3cc,4833,7c,31c0,f0,14cc,24cc,ff,3c7,20ff,23c7,3bb,4803,fc,90c0
  //   ,a0cc,b400,5400,9033,0,0,0,a000
endmodule
