// Digital circuit regdisplay.dig as structural Verilog
module regdisplay (
  input  [1:0] R,
  input  E,
  input  J,
  output [15:0] D1,
  output P1,
  output [15:0] D2,
  output P2
);

  wire [6:0] multiplexer_1_out, multiplexer_2_out, multiplexer_3_out, multiplexer_4_out, multiplexer_5_out;

  Multiplexer #(.Bits(7)) multiplexer_1 (.sel(E), .in_0(7'b0100000), .in_1(multiplexer_2_out), .out(multiplexer_1_out));
  Multiplexer #(.Bits(7)) multiplexer_2 (.sel(J), .in_0(7'b1010010), .in_1(7'b1010000), .out(multiplexer_2_out));
  Multiplexer #(.Selector_Bits(2), .Bits(7)) multiplexer_3 (
    .sel(R), .in_0(7'b0110000), .in_1(7'b0110001), .in_2(7'b0110010), .in_3(7'b0110011),
    .out(multiplexer_3_out));
  ROM #(.bigEndian("true"), .AddrBits(7), .Bits(16)) ASCII (.A(multiplexer_1_out), .sel(1'b1), .D(D1));
  Multiplexer #(.Bits(7)) multiplexer_4 (.sel(E), .in_0(7'b0100000), .in_1(multiplexer_5_out), .out(multiplexer_4_out));
  Multiplexer #(.Bits(7)) multiplexer_5 (.sel(J), .in_0(multiplexer_3_out), .in_1(7'b1000011), .out(multiplexer_5_out));
  ROM #(.bigEndian("true"), .AddrBits(7), .Bits(16)) ASCII_2 (.A(multiplexer_4_out), .sel(1'b1), .D(D2));

  assign P1 = 1'b0;
  assign P2 = 1'b0;

  // Notes on the sheet:
  //   contents of ASCII (hex, n*v repeats v):
  //   90ff,c,377,33f,38c,3bb,3fb,f,3ff,3bf,3cf,4a3f,f3,483f,3f3,1c3
  //   ,17*0,4800,4*0,2d79,4*0,4b00,0,300,0,0,90ff,c,377,33f,38c,3bb
  //   ,3fb,f,3ff,3bf,0,0,3000,0,8400,0,0,3cf,4a3f,f3,483f,3f3,1c3,2fb
  //   ,3cc,4833,7c,31c0,f0,14cc,24cc,ff,3c7,20ff,23c7,3bb,4803,fc,90c0
  //   ,a0cc,b400,5400,9033,0,0,0,a000
  //   contents of ASCII_2 (hex, n*v repeats v):
  //   90ff,c,377,33f,38c,3bb,3fb,f,3ff,3bf,3cf,4a3f,f3,483f,3f3,1c3
  //   ,17*0,4800,4*0,2d79,4*0,4b00,0,300,0,0,90ff,c,377,33f,38c,3bb
  //   ,3fb,f,3ff,3bf,0,0,3000,0,8400,0,0,3cf,4a3f,f3,483f,3f3,1c3,2fb
  //   ,3cc,4833,7c,31c0,f0,14cc,24cc,ff,3c7,20ff,23c7,3bb,4803,fc,90c0
  //   ,a0cc,b400,5400,9033,0,0,0,a000
endmodule
