// Digital circuit testsuite.dig as structural Verilog
module testsuite (
  input  clock,
  output [3:0] PC,
  output halt,
  output error
);

  frontpanel frontpanel_1 (.clock(clock), .PC(PC), .halt(halt), .error(error));  // open: R0, R1, R2, R3
endmodule

/* Test case add:
clock error halt

#include "../cpudef.asm"
#
# move r1, 5
# move r2, 3
# add r1, r2
# add r1, 2
# musteq r1, 10

program(0x051c, 0x032c, 0x0091, 0x0210, 0x0a1a)

let i = 0;
while(!(halt | error | (i >= 100)))
  let i = i + 1;
  0 0 0
  1 x x
end while
0 0 1
*/

/* Test case jump:
clock error halt

#include "../cpudef.asm"
#
#   jump one
# three:
#   add r0, r1
#   add r0, r2
#   jump end
# two:
#   move r2, 2
#   jump three
# one:
#   move r1, 3
#   jump two
# end:
#   musteq r0, 5


program(0x060e, 0x0041, 0x0081, 0x080e, 0x022c, 0x010e, 0x031c, 0x040e, 0x050a)

let i = 0;
while(!(halt | error | (i >= 100)))
  let i = i + 1;
  0 0 0
  1 x x
end while
0 0 1
*/
